# Fritzing sketch Sketch (saved by Fritzing 0.9.3b)
breadboards: 1

parts:
  U1 = Unproven! [package=msop-10]
  C1 = Capacitor Polarized [package=cpol-radial-10uf-25v]
  C2 = Capacitor [package=cap-pth-small-kit]
  R1 = Resistor [tolerance=±5% resistance=10k package="1206 [SMD]"]
  R2 = Resistor [tolerance=±5% resistance=10k package="1206 [SMD]"]
  Uno1 = chipKIT Uno32 [package="SIP (Single Inline) [THT]"]

nets:
  VDD: U1.VDD, C1.+, C2.2, R2.Pin_1, Uno1.3V3
  N1: U1.STAT1, R1.Pin_1
  N2: U1.STAT2, C1.-, C2.1, Uno1.GND
  N3: R1.Pin_0, Uno1.A4
  N4: R2.Pin_0, Uno1.A5

custom parts:
  chipKIT Uno32: Arduino-compatible prototyping platform
